// Logisim project alu.circ as structural Verilog: 2 circuits, main circuit main
module main (
  input  [1:0] in_1,
  input  [3:0] in_2,
  output [3:0] out_3
);

  wire and_1_out, not_1_out, not_2_out, or_1_out;

  or or_1 (or_1_out, in_2[3], in_2[0]);
  and and_1 (and_1_out, in_1[1], in_2[1]);
  not not_1 (not_1_out, in_1[1]);
  not not_2 (not_2_out, in_2[2]);
  or or_2 (out_3[2], in_1[0], and_1_out);
  or or_3 (out_3[1], not_1_out, not_2_out);
  and and_2 (out_3[0], in_1[1], or_1_out);

  assign out_3[3] = 1'b0;
endmodule

module control (
  input  [5:0] in_1,
  output RegDst,
  output ALUSrc,
  output MemToReg,
  output RegWrite,
  output MemRead,
  output MemWrite,
  output Branch,
  output AluOP1,
  output AluOp0
);

  wire not_1_out, not_2_out, not_3_out, not_4_out, not_5_out, not_6_out, not_7_out, not_8_out, not_9_out,
       not_10_out, not_11_out, not_12_out, not_13_out, not_14_out, not_15_out, not_16_out;

  not not_1 (not_1_out, in_1[2]);
  not not_2 (not_2_out, in_1[4]);
  not not_3 (not_3_out, in_1[1]);
  not not_4 (not_4_out, in_1[3]);
  not not_5 (not_5_out, in_1[5]);
  and and_1 (AluOP1, not_5_out, not_2_out, not_4_out, not_1_out, not_3_out, not_6_out);
  not not_6 (not_6_out, in_1[0]);
  not not_7 (not_7_out, in_1[3]);
  not not_8 (not_8_out, in_1[4]);
  and and_2 (MemRead, in_1[5], not_8_out, not_7_out, not_10_out, in_1[1], in_1[0]);
  not not_9 (not_9_out, in_1[4]);
  not not_10 (not_10_out, in_1[2]);
  not not_11 (not_11_out, in_1[2]);
  and and_3 (MemWrite, in_1[5], not_9_out, in_1[3], not_11_out, in_1[1], in_1[0]);
  not not_12 (not_12_out, in_1[5]);
  not not_13 (not_13_out, in_1[1]);
  not not_14 (not_14_out, in_1[4]);
  not not_15 (not_15_out, in_1[3]);
  not not_16 (not_16_out, in_1[0]);
  and and_4 (AluOp0, not_12_out, not_14_out, not_15_out, in_1[2], not_13_out, not_16_out);
  or or_1 (ALUSrc, MemRead, MemWrite);
  or or_2 (RegWrite, AluOP1, MemRead);

  assign Branch = AluOp0;
  assign MemToReg = MemRead;
  assign RegDst = AluOP1;
endmodule
